# Fritzing sketch mCore+WeMos (saved by Fritzing 0.9.3b)
breadboards: 1

parts:
  J3 = Generic female header - 7 pins [form="♀ (female)" package=THT]
  WeMos_D1_Mini1 = WeMos D1 Mini  # not connected
  LED1 = LED - 5mm [color="Red (633nm)" package="5 mm [THT]"]
  R1 = Resistor [tolerance=±5% resistance=470 package=THT]
  LED2 = LED - 5mm [color="Green (555nm)" package="5 mm [THT]"]
  R4 = Resistor [tolerance=±5% resistance=470 package=THT]

nets:
  N1: J3.pin3, J3.pin6, R4.Pin_1
  N2: J3.pin4, R1.Pin_1
  N3: LED1.anode, R4.Pin_0
  N4: R1.Pin_0, LED2.anode

custom parts:
  Generic female header - 7 pins: Generic female header
  WeMos D1 Mini: The D1 mini is a mini wifi board based on ESP-8266EX.
